# Fritzing sketch DerbyLaserTrip (saved by Fritzing 0.6.3b)
breadboards: 1

parts:
  Q1 = PNP-Transistor [package="TO92 [THT]"]
  R1 = Resistor [tolerance=±5% resistance=1k package=THT]
  Arduino1 = Arduino
  L1 = Solenoid
  LED1 = LED - 5mm [color="Red (633nm)" package="5 mm [THT]"]  # not connected
  R2 = Photocell (LDR) [package=THT]
  S1 = Pushbutton [package="[THT]"]
  R3 = Resistor [tolerance=±5% resistance=220 package=THT]

nets:
  N1: Q1.E, L1.pin2
  N2: Q1.B, R1.Pin_1
  N3: R1.Pin_0, Arduino1.D2
  N4: Arduino1.D0RX, R2.pin_0
  N5: R2.pin_1, R3.Pin_0
  N6: S1.Pin_2, R3.Pin_1
