# Fritzing sketch RemoteControl (saved by Fritzing 0.8.5b)
breadboards: 1

parts:
  Part1 = Arduino Mega 2560 (Rev3)
  LCD1 = LCD screen
  C1 = Electrolytic Capacitor [capacitance=0.1mF voltage=16V package="100 mil [THT, electrolytic]"]
  C2 = Electrolytic Capacitor [capacitance=1µF package="100 mil [THT, electrolytic]"]
  R2 = TRIMPOT [package=trimpot_pth_s3_lock]
  R3 = Resistor [tolerance=±5% resistance=330 package="0603 [SMD]"]
  U1 = SD_CARD_SOCKET [package=sdcard_4uconn]  # not connected
  S1 = Round Pushbutton
  S2 = Round Pushbutton
  S3 = Round Pushbutton
  SP1 = SPEAKER [package=pcb_mount_speaker]
  S4 = Toggle Switch [package=THT]
  MIRF1 = MIRF [package=mirf]  # not connected

nets:
  N1: Part1.3V3, C1.+
  5V: Part1.5V, LCD1.VDD, C2.+, R2.CW, R3.Pin_0
  GND: Part1.GND, LCD1.VSS, LCD1.R/W, LCD1.LED-, C1.-, C2.-, R2.CCW, S1.leg1, S2.leg1, S3.leg1, SP1.+, S4.COM
  N2: Part1.D3_PWM, S3.leg0
  N3: Part1.D5_PWM, SP1.-
  N4: Part1.D22, LCD1.RS
  N5: Part1.D24, LCD1.E
  N6: Part1.D26, LCD1.DB4
  N7: Part1.D28, LCD1.DB5
  N8: Part1.D30, LCD1.DB6
  N9: Part1.D32, LCD1.DB7
  N10: Part1.D34, S2.leg0
  N11: Part1.D35, S4.L1
  N12: Part1.D36, S1.leg0
  N13: Part1.D37, S4.L2
  N14: LCD1.V0, R2.WIPER
  N15: LCD1.LED+, R3.Pin_1

notes:
  Not in diagram:
  3-pos guitar pickup switch wired to GND + Mega pins 47-49
  Not in diagram:
  5-pos guitar pickup switch wired to GND + 42-44
  Not in diagram:
  SD board, has 2 columns of 8 twin pins.
  SD Col1:
  GND to BB GND rail
  5V to BB 5V rail
  3.3V *open*
  CS to Mega 11
  MOSI, SCK, MISO to Mega ICSP counterparts
  GND to BB GND - SD has 4 GND pins, I plugged the 2 from column 1(/2) to Mega GND - redundant?
  SD Col 2: MOSI, SCK, MISO to RF24 counterparts
  All remaining col2 pins left *open* (2 GNDs, 3.3V, 5V, CS)
  Not in diagram:
  Addicore nRF24L01+ (8 pins in 2x4 arrangement) (RF24):
  RF24 GND to BB -> neg terminal of 100uf cap -> BB GND
  RF24 VCC to BB -> pos terminal of 100uf cap -> Mega 3.3V+ (NOT the 5V BB rail!)
  RF24 CSN to Mega pin 8
  RF24 CE to Mega pin 7
  RF24 IRQ to Mega pin 2
  RF24 MOSI, SCK, MISO to SD counterparts (RF24 <=> SD <=> Mega ICSP)
