# Fritzing sketch SignalBoard (saved by Fritzing 0.8.5b)
perfboards: 1

parts:
  J1 = female pin header, 2 pins [form="♀ (female)"]
  SPKR1 = Loudspeaker
  Part1 = Arduino Leonardo (Rev3b)
  JP2 = Header 10 [package=1x10-2mm-smd]
  C1 = Electrolytic Capacitor [capacitance=10µF voltage=50V package="100 mil [THT, electrolytic]"]
  JP5 = Header 10 [package=1x10-2mm-smd]
  JP6 = Header 10 [package=1x10-2mm-smd]
  U1 = mystery part, 3 pins [chip_label=?]

nets:
  N1: J1.pin1, SPKR1.pin2, Part1.D5_PWM
  N2: J1.pin2, SPKR1.pin1
  N3: Part1.D2/SDA, JP2.8-IRQ
  N4: Part1.D6_PWM/A7, U1.pin2
  N5: Part1.D7, JP2.3-CE
  N6: Part1.3V3, JP2.2-VCC_3.3v, C1.-
  N7: Part1.GND, C1.+, JP5.1-GND, U1.pin1
  N8: Part1.D8/A8, JP2.4-CSN
  N9: Part1.D10_PWM/A10, JP5.4-CSN
  N10: JP2.1-GND, JP5.8-IRQ
  N11: JP2.5-SCK, JP6.5-SCK
  N12: JP2.6-MOSI, JP6.6-MOSI
  N13: JP2.7-MISO, JP6.7-MISO
  N14: JP6.1-GND, JP6.8-IRQ

custom parts:
  Header 10: Header 10 Standard 10-pin 0.1 header. Use with straight break away headers (SKU : PRT-00116), right angle break away headers (PRT-00553), swiss pins (PRT-00743), machine pins (PRT-00117), and female headers (PRT-00115).
  Header 10: Header 10 Standard 10-pin 0.1 header. Use with straight break away headers (SKU : PRT-00116), right angle break away headers (PRT-00553), swiss pins (PRT-00743), machine pins (PRT-00117), and female headers (PRT-00115).
